# Fritzing sketch dht (saved by Fritzing 0.8.5b)
breadboards: 1

parts:
  Bauteil1 = Arduino Uno (Rev3)
  DHT11 = Humidity and Temperature Sensor RHT03
  R1 = Resistor [tolerance=±5% resistance=1k package=THT]

nets:
  N1: Bauteil1.GND, DHT11.GND_2
  N2: Bauteil1.D5_PWM, DHT11.Data-signal, R1.Pin_1
  5V: Bauteil1.5V, DHT11.Vcc, R1.Pin_0

notes:
  1kΩ Resistor
  DHT11
